// Logisim project main.circ as structural Verilog: 1 circuit, main circuit main
module main (
  input  [7:0] A,
  input  [7:0] B,
  input  [7:0] OPCODE,
  output [7:0] Out,
  output [3:0] Out_flags
);

  wire adder_2_cout, subtractor_2_bout;
  wire [7:0] adder_1_out, adder_2_out, negator_1_out, subtractor_1_out, subtractor_2_out;

  Adder adder_1 (.a(A), .b(B), .out(adder_1_out));  // open: cin, cout
  Adder adder_2 (.a(A), .b(B), .out(adder_2_out), .cin(OPCODE[4]), .cout(adder_2_cout));
  Subtractor subtractor_1 (.a(A), .b(B), .out(subtractor_1_out));  // open: bin, bout
  Subtractor subtractor_2 (.a(A), .b(B), .out(subtractor_2_out), .bin(OPCODE[4]), .bout(subtractor_2_bout));
  Negator negator_1 (.in(A), .out(negator_1_out));
  Multiplexer #(.select(4), .width(8), .enable("false")) multiplexer_1 (
    .in0(adder_1_out), .in1(adder_2_out), .in2(subtractor_1_out), .in3(subtractor_2_out),
    .in4(negator_1_out), .out(Out), .sel(OPCODE[3:0]));  // open: in5, in6, in7, in8, in9, in10, in11, in12, in13, in14, in15
  Multiplexer #(.select(4), .enable("false")) multiplexer_2 (
    .in1(adder_2_cout), .in3(subtractor_2_bout), .out(Out_flags[0]), .sel(OPCODE[3:0]));  // open: in0, in2, in4, in5, in6, in7, in8, in9, in10, in11, in12, in13, in14, in15

  // Other names for the same wires on the sheet: Carry_in = OPCODE[4]

  // Notes on the sheet:
  //   ALU interface
  //   Last 4 bits - function$OPCODE[4] = carry in$OPCODE[5] = left / right shift$Indexing starts from 0, RTL
  //   - carry out$- overflow$- zero$- negative
endmodule
